// Logisim project 2bitcomparator.circ as structural Verilog: 1 circuit, main circuit main
module main (
  input  [1:0] in_1,
  input  [1:0] in_2,
  output out_3,
  output out_4,
  output out_5
);

  wire main_1_a_b, main_1_a_b_2, main_1_a_b_3, main_2_a_b, main_2_a_b_2, main_2_a_b_3;

  _1bitcomparator_main main_1 (
    .in_1(in_1[0]), .in_2(in_2[0]), .A_B(main_1_a_b), .A_B_2(main_1_a_b_2), .A_B_3(main_1_a_b_3));
  _1bitcomparator_main main_2 (
    .in_1(in_1[1]), .in_2(in_2[1]), .A_B(main_2_a_b), .A_B_2(main_2_a_b_2), .A_B_3(main_2_a_b_3));
  and and_1 (out_3, main_1_a_b, main_2_a_b);
  and and_2 (out_4, main_1_a_b_2, main_2_a_b_2);
  and and_3 (out_5, main_1_a_b_3, main_2_a_b_3);
endmodule
