// Logisim project 2x1mux.circ as structural Verilog: 1 circuit, main circuit main
module main (
  input  b,
  input  A,
  input  in_3,
  output out_4
);

  wire nand_1_out, nand_2_out, nand_3_out;

  nand nand_1 (nand_1_out, in_3, in_3);
  nand nand_2 (nand_2_out, b, in_3);
  nand nand_3 (nand_3_out, nand_1_out, A);
  nand nand_4 (out_4, nand_2_out, nand_3_out);
endmodule
