// Logisim project 4x1mux.circ as structural Verilog: 1 circuit, main circuit main
module main (
  input  D,
  input  C,
  input  B,
  input  A,
  input  [1:0] sel,
  output \output 
);

  wire main_1_out_4, main_2_out_4;

  _2x1mux_main main_1 (.b(D), .A(C), .in_3(sel[0]), .out_4(main_1_out_4));
  _2x1mux_main main_2 (.b(B), .A(A), .in_3(sel[0]), .out_4(main_2_out_4));
  _2x1mux_main main_3 (.b(main_1_out_4), .A(main_2_out_4), .in_3(sel[1]), .out_4(\output ));
endmodule
