// Logisim project 4x1muxIC.circ as structural Verilog: 1 circuit, main circuit main
module main (
  input  A,
  input  B,
  input  C,
  input  D,
  input  [1:0] sel,
  output \output 
);

  _4x1mux_main main_1 (.D(D), .C(C), .B(B), .A(A), .sel(sel), .\output (\output ));

  // Notes on the sheet:
  //   4x1 mux
endmodule
