// Logisim project D-FlipFlopMultiBits.circ as structural Verilog: 1 circuit, main circuit main
module main (
  input  in_1,
  input  in_2,
  input  in_3,
  output out_4,
  output out_5,
  output out_6,
  output out_7,
  output out_8,
  output out_9,
  output out_10,
  output out_11,
  output out_12,
  output out_13,
  output out_14,
  output out_15
);

  wire clock_1_out, clock_2_out, clock_3_out;

  Clock clock_1 (.out(clock_1_out));
  Clock clock_2 (.out(clock_2_out));
  Clock clock_3 (.out(clock_3_out));
  // DflipFlopSingleBit_main main_1: pin names not known; wires that end beside it: in_1, clock_1_out, out_4
  // DflipFlopSingleBit_main main_2: pin names not known; wires that end beside it: in_2, clock_2_out, out_8
  // DflipFlopSingleBit_main main_3: pin names not known; wires that end beside it: in_3, clock_3_out, out_12
  // DflipFlopSingleBit_main main_4: pin names not known; wires that end beside it: out_4, clock_1_out, out_5
  // DflipFlopSingleBit_main main_5: pin names not known; wires that end beside it: in_2, clock_2_out, out_9
  // DflipFlopSingleBit_main main_6: pin names not known; wires that end beside it: in_3, clock_3_out, out_13
  // DflipFlopSingleBit_main main_7: pin names not known; wires that end beside it: out_5, clock_1_out, out_6
  // DflipFlopSingleBit_main main_8: pin names not known; wires that end beside it: in_2, clock_2_out, out_10
  // DflipFlopSingleBit_main main_9: pin names not known; wires that end beside it: in_3, clock_3_out, out_14
  // DflipFlopSingleBit_main main_10: pin names not known; wires that end beside it: out_6, clock_1_out, out_7
  // DflipFlopSingleBit_main main_11: pin names not known; wires that end beside it: in_2, clock_2_out, out_11
  // DflipFlopSingleBit_main main_12: pin names not known; wires that end beside it: in_3, clock_3_out, out_15

  // Notes on the sheet:
  //   serail in & serial out
  //   Parallel in Parallel Out
  //   Parallel in Serial Out
endmodule
