// Logisim project halfAdder.circ as structural Verilog: 1 circuit, main circuit main
module main (
  input  in_1,
  input  in_2,
  input  a,
  input  b,
  input  Cin,
  output out_6,
  output out_7,
  output Sum,
  output Cout
);

  wire and_2_out, and_3_out, xor_2_out;

  and and_1 (out_6, in_1, in_2);
  xor xor_1 (out_7, in_2, in_1);
  xor xor_2 (xor_2_out, a, b);
  xor xor_3 (Sum, xor_2_out, Cin);
  and and_2 (and_2_out, Cin, xor_2_out);
  and and_3 (and_3_out, b, a);
  or or_1 (Cout, and_2_out, and_3_out);
endmodule
