// Logisim project 3rd session merl.circ as structural Verilog: 4 circuits, main circuit main
module main (
  output out_1,
  output out_2,
  output out_3,
  output out_4
);

  wire clock_1_out, d_ff_1_qn, d_ff_2_qn, d_ff_3_qn, d_ff_4_qn, xor_1_out, xor_2_out, xor_3_out;

  Clock clock_1 (.out(clock_1_out));
  D_Flip_Flop d_ff_1 (.clk(clock_1_out), .D(d_ff_1_qn), .Q(out_4), .Qn(d_ff_1_qn));  // open: preset, en, reset
  D_Flip_Flop d_ff_2 (.clk(clock_1_out), .D(xor_1_out), .Q(out_3), .Qn(d_ff_2_qn));  // open: preset, en, reset
  xor xor_1 (xor_1_out, d_ff_1_qn, d_ff_2_qn);
  xor xor_2 (xor_2_out, d_ff_2_qn, d_ff_3_qn);
  D_Flip_Flop d_ff_3 (.clk(clock_1_out), .D(xor_2_out), .Q(out_2), .Qn(d_ff_3_qn));  // open: preset, en, reset
  D_Flip_Flop d_ff_4 (.clk(clock_1_out), .D(xor_3_out), .Q(out_1), .Qn(d_ff_4_qn));  // open: preset, en, reset
  xor xor_3 (xor_3_out, d_ff_3_qn, d_ff_4_qn);
endmodule

module _3_bit_Asynchoronus_counter (
  output out_1,
  output out_2,
  output out_3
);

  wire clock_1_out, d_ff_1_qn, d_ff_2_qn, d_ff_3_qn;

  Clock clock_1 (.out(clock_1_out));
  D_Flip_Flop d_ff_1 (.clk(clock_1_out), .D(d_ff_1_qn), .Q(out_3), .Qn(d_ff_1_qn));  // open: preset, en, reset
  D_Flip_Flop d_ff_2 (.clk(d_ff_1_qn), .D(d_ff_2_qn), .Q(out_2), .Qn(d_ff_2_qn));  // open: preset, en, reset
  D_Flip_Flop d_ff_3 (.clk(d_ff_2_qn), .D(d_ff_3_qn), .Q(out_1), .Qn(d_ff_3_qn));  // open: preset, en, reset
endmodule

module _2_bit_synchoronus_counter (
  output out_1,
  output out_2
);

  wire clock_1_out, d_ff_1_qn, d_ff_2_qn, xor_1_out;

  Clock clock_1 (.out(clock_1_out));
  D_Flip_Flop d_ff_1 (.clk(clock_1_out), .D(d_ff_1_qn), .Q(out_2), .Qn(d_ff_1_qn));  // open: preset, en, reset
  D_Flip_Flop d_ff_2 (.clk(clock_1_out), .D(xor_1_out), .Q(out_1), .Qn(d_ff_2_qn));  // open: preset, en, reset
  xor xor_1 (xor_1_out, d_ff_1_qn, d_ff_2_qn);
endmodule

module _4_bit_synchoronus_counter (
  output out_1,
  output out_2,
  output out_3,
  output out_4
);

  wire clock_1_out, d_ff_1_qn, d_ff_2_qn, d_ff_3_qn, d_ff_4_qn, xor_1_out, xor_2_out;

  Clock clock_1 (.out(clock_1_out));
  D_Flip_Flop d_ff_1 (.clk(clock_1_out), .D(d_ff_1_qn), .Q(out_4), .Qn(d_ff_1_qn));  // open: preset, en, reset
  D_Flip_Flop d_ff_2 (.clk(clock_1_out), .D(xor_1_out), .Q(out_3), .Qn(d_ff_2_qn));  // open: preset, en, reset
  xor xor_1 (xor_1_out, d_ff_1_qn, d_ff_2_qn);
  D_Flip_Flop d_ff_3 (.clk(clock_1_out), .D(d_ff_3_qn), .Q(out_2), .Qn(d_ff_3_qn));  // open: preset, en, reset
  D_Flip_Flop d_ff_4 (.clk(clock_1_out), .D(xor_2_out), .Q(out_1), .Qn(d_ff_4_qn));  // open: preset, en, reset
  xor xor_2 (xor_2_out, d_ff_3_qn, d_ff_4_qn);
endmodule
