// Logisim project pc.circ as structural Verilog: 1 circuit, main circuit main
module main (
  input  in_1,
  output [31:0] out_2
);

  wire clock_1_out;
  wire [31:0] adder_1_out, register_1_q;

  Clock clock_1 (.out(clock_1_out));
  Register #(.width(32)) register_1 (.D(adder_1_out), .Q(register_1_q), .clk(clock_1_out), .clr(in_1));  // open: en
  Adder #(.width(32)) adder_1 (.a(32'h4), .b(register_1_q), .out(adder_1_out));  // open: cin, cout
  ROM #(.addrWidth(20), .dataWidth(32)) rom_1 (.addr(register_1_q[21:2]), .data(out_2));  // open: sel

  // Notes on the sheet:
  //   FETCH UNIT
  //   contents of rom_1 (hex, n*v repeats v):
  //   11111111
endmodule
